# Fritzing sketch ArduinoISP2-Ladyada (saved by Fritzing 0.8.7b)
circuit board: 5.03294cm x 5.31518cm
breadboards: 1

parts:
  U1 = atmega328 [package=dip]
  R1 = Resistor [tolerance=±5% resistance=220 package=THT]
  part = atmega328 [package=dip]  # not connected
  Bauteil1 = Arduino Uno (Rev3)

nets (from the pcb view):
  N1: U1.RESET, R1.Pin_0, Bauteil1.D10_PWM/SS
  VCC: U1.VCC, U1.AVCC, R1.Pin_1, Bauteil1.5V
  N2: U1.XLAT1, Bauteil1.D9_PWM
  N3: U1.D11_(PWM), Bauteil1.D11_PWM/MOSI
  N4: U1.D12, Bauteil1.D12/MISO
  N5: U1.D13, Bauteil1.D13/SCK
