# Fritzing sketch gbMon2 (saved by Fritzing 0.8.3b)
circuit board: 8.53719cm x 5.62327cm
circuit board: 4.57193cm x 4.07417cm
breadboards: 4

parts:
  XTAL1 = Crystal [frequency="16 Mhz" package=SMD]
  ICL7660 = ICL7660 [chip_label=ICL7660 package="DIP (Dual Inline) [THT]"]
  atmega328P_LCD = atmega328P [package=dip]
  C3 = Ceramic Capacitor [capacitance=10µF voltage=16V package="100 mil [THT, multilayer]"]
  C4 = Ceramic Capacitor [capacitance=10µF voltage=16V package="100 mil [THT, multilayer]"]
  C2 = Ceramic Capacitor [capacitance=22pF package="100 mil [THT, multilayer]"]
  C1 = Ceramic Capacitor [capacitance=22pF package="100 mil [THT, multilayer]"]
  Reset_LCD = Pushbutton [package="[THT]"]
  R2 = Resistor [tolerance=±5% resistance=220 package=THT]
  RF434 = RF 434Mhz Transmitter [package=rf-link_tx]
  DHT22 = DHT22 Humidity and Temperature Sensor
  R3 = Resistor [tolerance=±5% resistance=10k package=THT]
  DS1 = DS18B20 1-Wire Temperature Sensor [part_number=DS18B20]
  R4 = Resistor [tolerance=±5% resistance=4.7k package=THT]
  atmega328P_IO = atmega328P [package=dip]
  C5 = Ceramic Capacitor [capacitance=22pF package="100 mil [THT, multilayer]"]
  C6 = Ceramic Capacitor [capacitance=22pF package="100 mil [THT, multilayer]"]
  XTAL2 = Crystal [frequency="16 Mhz" package=SMD]
  R5 = Resistor [tolerance=±5% resistance=220 package=THT]
  Reset_IO = Pushbutton [package="[THT]"]
  Left = Pushbutton [package="[THT]"]
  Up = Pushbutton [package="[THT]"]
  Down = Pushbutton [package="[THT]"]
  Right = Pushbutton [package="[THT]"]
  R7 = Resistor [tolerance=±5% resistance=10k package=THT]
  OK = Pushbutton [package="[THT]"]
  Menu = Pushbutton [package="[THT]"]
  Debug = female pin header, 2 pins [form="♀ (female)"]
  R1 = Trimmer Potentiometer [maximum_resistance=10kΩ package=THT]
  R8 = Resistor [tolerance=±5% resistance=10k package=THT]
  R9 = Resistor [tolerance=±5% resistance=10k package=THT]
  R10 = Resistor [tolerance=±5% resistance=10k package=THT]
  Graphic_Display = double row male pin header, 20 pins [form="♂ (male)"]
  Buttons = female pin header, 7 pins [form="♀ (female)"]
  Debug_IO = female pin header, 3 pins [form="♀ (female)"]
  R11 = Resistor [tolerance=±5% resistance=10k package=THT]
  D9_D10 = female pin header, 3 pins [form="♀ (female)"]
  Raspberry_Pi_rev1 = Raspberry Pi rev2
  Connector = shrouded pin header, 28 pins [form="♂ (shrouded male)"]
  gLCD_Display = male pin header, 20 pins [form="♂ (male)"]
  J1 = shrouded pin header, 10 pins [form="♂ (shrouded male)"]  # not connected
  DHT22_2 = molex pin header, 3 pins [form=molex]
  DS18b20_1 = molex pin header, 3 pins [form=molex]
  DS18b20_3 = molex pin header, 3 pins [form=molex]
  DS18b20 = molex pin header, 3 pins [form=molex]
  Debug_LCD = female pin header, 3 pins [form="♀ (female)"]
  A0 = molex pin header, 2 pins [form=molex]
  A1 = molex pin header, 2 pins [form=molex]
  A4 = molex pin header, 2 pins [form=molex]
  A3 = molex pin header, 2 pins [form=molex]
  A2 = molex pin header, 2 pins [form=molex]
  LED1 = LED - 3mm [color="Green (565nm)" package="3 mm [THT]"]
  R12 = Resistor [tolerance=±5% resistance=220 package=THT]

nets:
  N1: XTAL1.pin_0, atmega328P_LCD.XLAT1, C1.1
  N2: XTAL1.pin_1, atmega328P_LCD.XLAT2, C2.0
  N3: ICL7660.CAP+, C3.1
  GND: ICL7660.GND, atmega328P_LCD.GND, C4.0, C2.1, C1.0, Reset_LCD.Pin_3, Reset_LCD.Pin_4, RF434.GND, DHT22.GND, DS1.GND, atmega328P_IO.GND, C5.1, C6.0, Reset_IO.Pin_3, Reset_IO.Pin_4, Left.Pin_3, Left.Pin_4, Up.Pin_3, Up.Pin_4, Down.Pin_3, Down.Pin_4, Right.Pin_3, Right.Pin_4, R7.Pin_0, OK.Pin_3, OK.Pin_4, Menu.Pin_3, Menu.Pin_4, R1.leg1, R8.Pin_0, R9.Pin_0, R10.Pin_0, Graphic_Display.pin2, Graphic_Display.pin18, Graphic_Display.pin20, Buttons.pin7, Debug_IO.pin3, R11.Pin_0, D9_D10.pin3, Raspberry_Pi_rev1.GND, Connector.pin27, DHT22_2.pin3, DS18b20_1.pin1, DS18b20_3.pin1, DS18b20.pin1, Debug_LCD.pin3, LED1.cathode
  N4: ICL7660.CAP-, C3.0
  N5: ICL7660.V_out, C4.1, Graphic_Display.pin3
  N6: ICL7660.V+, R1.wiper
  N7: atmega328P_LCD.RESET, Reset_LCD.Pin_1, Reset_LCD.Pin_2, R2.Pin_0
  N8: atmega328P_LCD.D0_(RX), Debug_LCD.pin1
  N9: atmega328P_LCD.D1_(TX), Debug_LCD.pin2
  N10: atmega328P_LCD.D2, Raspberry_Pi_rev1.GPIO_22
  N11: atmega328P_LCD.D3_(PWM), Raspberry_Pi_rev1.GPIO_17
  N12: atmega328P_LCD.D4, Graphic_Display.pin8
  VCC: atmega328P_LCD.VCC, atmega328P_LCD.AVCC, R2.Pin_1, R1.leg2, Graphic_Display.pin1, Graphic_Display.pin14, Graphic_Display.pin19, Raspberry_Pi_rev1.5V
  N13: atmega328P_LCD.D5_(PWM), Graphic_Display.pin9
  N14: atmega328P_LCD.D6_(PWM), Graphic_Display.pin10
  N15: atmega328P_LCD.D7, Graphic_Display.pin11
  N16: atmega328P_LCD.D8, Graphic_Display.pin4
  N17: atmega328P_LCD.D9_(PWM), Graphic_Display.pin5
  N18: atmega328P_LCD.D10_(PWM), Graphic_Display.pin6
  N19: atmega328P_LCD.D11_(PWM), Graphic_Display.pin7
  N20: atmega328P_LCD.D13, R12.Pin_0
  N21: atmega328P_LCD.A0, Graphic_Display.pin12
  N22: atmega328P_LCD.A1, Graphic_Display.pin13
  N23: atmega328P_LCD.A2, Graphic_Display.pin15
  N24: atmega328P_LCD.A3, Graphic_Display.pin16
  N25: atmega328P_LCD.A4, Graphic_Display.pin17
  N26: RF434.DATA, Raspberry_Pi_rev1.GPIO_27
  VDD: RF434.+5V, DHT22.VDD, R3.Pin_1, DS1.VDD, R4.Pin_1, atmega328P_IO.VCC, atmega328P_IO.AVCC, R5.Pin_1, Raspberry_Pi_rev1.3V3, DHT22_2.pin1, DS18b20_1.pin3, DS18b20_3.pin3, DS18b20.pin3
  N27: DHT22.DATA, R3.Pin_0, Raspberry_Pi_rev1.GPIO_18, DHT22_2.pin2
  N28: DS1.DQ, R4.Pin_0, Raspberry_Pi_rev1.GPIO_23, DS18b20_1.pin2, DS18b20_3.pin2, DS18b20.pin2
  N29: atmega328P_IO.RESET, R5.Pin_0, Reset_IO.Pin_1, Reset_IO.Pin_2
  N30: atmega328P_IO.D0_(RX), Debug_IO.pin1
  N31: atmega328P_IO.D1_(TX), Debug_IO.pin2
  N32: atmega328P_IO.D2, Raspberry_Pi_rev1.GPIO4
  N33: atmega328P_IO.D3_(PWM), Raspberry_Pi_rev1.GPIO_24
  N34: atmega328P_IO.D4, OK.Pin_1, OK.Pin_2, Buttons.pin6, Connector.pin26
  N35: atmega328P_IO.XLAT1, C6.1, XTAL2.pin_0
  N36: atmega328P_IO.XLAT2, C5.0, XTAL2.pin_1
  N37: atmega328P_IO.D5_(PWM), Menu.Pin_1, Menu.Pin_2, Buttons.pin5, Connector.pin25
  N38: atmega328P_IO.D6_(PWM), Left.Pin_1, Left.Pin_2, Buttons.pin4, Connector.pin24
  N39: atmega328P_IO.D7, Up.Pin_1, Up.Pin_2, Buttons.pin3, Connector.pin23
  N40: atmega328P_IO.D8, Down.Pin_1, Down.Pin_2, Buttons.pin2, Connector.pin22
  N41: atmega328P_IO.D9_(PWM), Right.Pin_1, Right.Pin_2, Buttons.pin1, Connector.pin21
  N42: atmega328P_IO.D10_(PWM), D9_D10.pin2
  N43: atmega328P_IO.D11_(PWM), D9_D10.pin1
  N44: atmega328P_IO.D12, Debug.pin2
  N45: atmega328P_IO.D13, Debug.pin1
  N46: atmega328P_IO.A0, A0.pin2
  N47: atmega328P_IO.A1, A1.pin2
  N48: atmega328P_IO.A2, A2.pin2
  N49: atmega328P_IO.A3, A3.pin2
  N50: atmega328P_IO.A4, A4.pin2
  N51: R7.Pin_1, A0.pin1
  N52: R8.Pin_1, A1.pin1
  N53: R9.Pin_1, R10.Pin_1, A3.pin1, A2.pin1
  N54: R11.Pin_1, A4.pin1
  N55: Connector.pin1, gLCD_Display.pin1
  N56: Connector.pin2, gLCD_Display.pin2
  N57: Connector.pin3, gLCD_Display.pin3
  N58: Connector.pin4, gLCD_Display.pin4
  N59: Connector.pin5, gLCD_Display.pin5
  N60: Connector.pin6, gLCD_Display.pin6
  N61: Connector.pin7, gLCD_Display.pin7
  N62: Connector.pin8, gLCD_Display.pin8
  N63: Connector.pin9, gLCD_Display.pin9
  N64: Connector.pin10, gLCD_Display.pin10
  N65: Connector.pin11, gLCD_Display.pin11
  N66: Connector.pin12, gLCD_Display.pin12
  N67: Connector.pin13, gLCD_Display.pin13
  N68: Connector.pin14, gLCD_Display.pin14
  N69: Connector.pin15, gLCD_Display.pin15
  N70: Connector.pin16, gLCD_Display.pin16
  N71: Connector.pin17, gLCD_Display.pin17
  N72: Connector.pin18, gLCD_Display.pin18
  N73: Connector.pin19, gLCD_Display.pin19
  N74: Connector.pin20, gLCD_Display.pin20
  N75: LED1.anode, R12.Pin_1

notes:
  1
  20
  EN
  D / I
  R / W
  CS 1 / 2
  gbMon2 lcdBridge
  5V Rot
  Noch Platz für 3 LEDs
  Parts List:
  1x ATmega328p-pu
  1x ICL7660
  1x Pushbutton
  1x Crystal 16MHz
  2x Capacitor 10uF
  2x Capacitor 22pF
  1x Potentionmeter 10k Ohm
  1x Resistor 220 Ohm
  1x Pin Header Female 2x1
  1x Pin Header Male 20x1
  Direkt an Raspberry Pi angeschlossen
  3.3V Rot gestrichelt
  5V Rot
  Parts List:
  1x RF 434Mhz Transmitter
  1x DHT22 Temp + Humidity Sensor
  5x DS18b20 Temperature Sensor
  1x Resistor 10k Ohm
  1x Resistor 4,7k Ohm
  gbMon2 ioBridge
  3.3V Rot gestrichelt
  7x Pushbutton
  1x Resistor 220 Ohm
  1x Resistor 10k Ohm
  1x LDR
  1x Crystal 16Mhz
  2x Capacitor 22pF
  2x Pin Header Female 2x1
  GND
  D9
  D10
  TX
  RX

custom parts:
  atmega328P: Atmel ATmega328P microcontroller.
  RF 434Mhz Transmitter: RF 434Mhz Transmitter with 3 PINs internal antenna
